# Fritzing sketch BattleTank (saved by Fritzing 1.0.4)
circuit board: 8.46667cm x 5.64444cm

parts:
  A1 = Adafruit v1.2 motor shield
  Mod1 = KY-008 Laser Transmitter Module [package="Breakout board"]
  M1 = gear-motor
  M2 = gear-motor
  Mod3 = laser receiver [package=THT]
  A2 = ESP32 DevKitc V4
  VCC1 = Battery
  BAT1 = 18650 battery holder [package=battery-18650-kit]
  M3 = Dagu DGServo 9g (Pan and tilt) [part_number=RS001B]
  M4 = Dagu DGServo 9g (Pan and tilt) [part_number=RS001B]

nets:
  N1: A1.Pin_1, M2.pin_2
  N2: A1.Pin_2, M2.pin_1
  N3: A1.Pin_4, M1.pin_2
  N4: A1.Pin_5, M1.pin_1
  N5: A1.Pin_6, VCC1.+
  GND: A1.Pin_7, A1.Pin_11, A1.Pin_23, A1.Pin_34, A1.Pin_36, A1.Pin_37, A1.Pin_63, A1.Pin_67, A1.Pin_70, Mod1.-, Mod3.pin1, A2.Pin_14, VCC1.-, M3.gnd, M4.gnd
  VCC: A1.Pin_10, A1.Pin_15, A1.Pin_16, A1.Pin_17, A1.Pin_22, A1.Pin_27, A1.Pin_28, A1.Pin_40, A1.Pin_42, A1.Pin_66, A1.Pin_69, Mod1.S, Mod1.NC, Mod3.pin2, Mod3.pin3, M3.vcc, M4.vcc
  N6: A1.Pin_18, A1.Pin_30, A2.Pin_28
  N7: A1.Pin_19, A1.Pin_31, A2.Pin_27
  N8: A1.Pin_58, A1.Pin_65, M3.pulse
  N9: A1.Pin_68, M4.pulse
  N10: A2.Pin_19, BAT1.+

custom parts:
  Adafruit v1.2 motor shield: Adafruit v1.2 motor shield.
  KY-008 Laser Transmitter Module: KY-008 Laser Transmitter Module, emits a dot shaped red laser beam.
  laser receiver: Generic non modulated laser receiver module.
  ESP32 DevKitc V4: ESP32-DevKitC board with ESP32-WROOM-32 module. ESP32-DevKitC V4 is a small-sized ESP32-based development board produced by Espressif. Most of the pins on the ESP module are broken out to the pin headers on the board. The pins D0, D1, D2, D3, CMD and CLK are used internally for communication between ESP32 and SPI flash memory. They are grouped on both sides near the USB connector. Avoid using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
  Battery: Your standard 2x 18650 battery pack (7.4 Volts)
  18650 battery holder: 18650 Battery
